// Logisim project 3-seven segments.circ as structural Verilog: 15 circuits, main circuit main
module main (
  input  [7:0] in_1,
  input  [7:0] in_2
);

  wire clock_1_out, clock_2_out, comparator_1_eq, counter_1_carry, n_bit_control_1_change_in_input,
       n_bit_control_1_clk, n_bit_control_1_clk_2, n_bit_control_1_clr, n_bit_control_1_clr_2,
       n_bit_control_1_enable, n_bit_control_1_enable_2, n_bit_control_1_load, n_bit_control_1_load_2,
       n_bit_control_1_ticker, n_bit_double_dabble_2_clear_2, n_bit_double_dabble_2_clock_2,
       n_bit_double_dabble_2_enable_2, n_bit_double_dabble_2_greater_than_three_out_1,
       n_bit_double_dabble_2_greater_than_three_out_2, n_bit_double_dabble_2_load_2,
       n_bit_double_dabble_2_shift_out, n_bit_double_dabble_3_clear_2, n_bit_double_dabble_3_clock_2,
       n_bit_double_dabble_3_enable_2, n_bit_double_dabble_3_greater_than_three_out_1,
       n_bit_double_dabble_3_greater_than_three_out_2, n_bit_double_dabble_3_load_2,
       n_bit_double_dabble_3_shift_out, n_bit_double_dabble_4_greater_than_three_out_1, not_1_out,
       seven_segment_controller_1_a, seven_segment_controller_1_b, seven_segment_controller_1_c,
       seven_segment_controller_1_d, seven_segment_controller_1_e, seven_segment_controller_1_f,
       seven_segment_controller_1_g, seven_segment_controller_2_a, seven_segment_controller_2_b,
       seven_segment_controller_2_c, seven_segment_controller_2_d, seven_segment_controller_2_e,
       seven_segment_controller_2_f, seven_segment_controller_2_g, seven_segment_controller_3_a,
       seven_segment_controller_3_b, seven_segment_controller_3_c, seven_segment_controller_3_d,
       seven_segment_controller_3_e, seven_segment_controller_3_f, seven_segment_controller_3_g,
       seven_segment_controller_4_a, seven_segment_controller_4_b, seven_segment_controller_4_c,
       seven_segment_controller_4_d, seven_segment_controller_4_e, seven_segment_controller_4_f,
       seven_segment_controller_4_g, seven_segment_controller_5_a, seven_segment_controller_5_b,
       seven_segment_controller_5_c, seven_segment_controller_5_d, seven_segment_controller_5_e,
       seven_segment_controller_5_f, seven_segment_controller_5_g, seven_segment_controller_6_a,
       seven_segment_controller_6_b, seven_segment_controller_6_c, seven_segment_controller_6_d,
       seven_segment_controller_6_e, seven_segment_controller_6_f, seven_segment_controller_6_g,
       shift_register_1_out;
  wire [3:0] n_bit_double_dabble_2_result, n_bit_double_dabble_3_result, n_bit_double_dabble_4_result;
  wire [7:0] multiplexer_1_out, register_1_q, shift_register_1_q0;
  wire [9:0] double_dabble_2_1_result;

  Clock clock_1 (.out(clock_1_out));
  Clock clock_2 (.out(clock_2_out));
  Comparator comparator_1 (.a(in_2), .b(register_1_q), .eq(comparator_1_eq));  // open: gt, lt
  Register register_1 (.en(not_1_out), .Q(register_1_q), .clk(clock_1_out), .clr(n_bit_control_1_clr_2));  // open: D
  not not_1 (not_1_out, comparator_1_eq);
  double_dabble__2 double_dabble_2_1 (
    .\input (in_1), .clock(clock_2_out), .result(double_dabble_2_1_result));  // open: done
  n_bit_control n_bit_control_1 (
    .greaterthanthree(n_bit_double_dabble_2_greater_than_three_out_1), .clock(clock_1_out),
    .Load(n_bit_control_1_load), .Enable(n_bit_control_1_enable), .clk(n_bit_control_1_clk),
    .clr(n_bit_control_1_clr), .change_in_input(n_bit_control_1_change_in_input),
    .Load_2(n_bit_control_1_load_2), .Enable_2(n_bit_control_1_enable_2), .clk_2(n_bit_control_1_clk_2),
    .clr_2(n_bit_control_1_clr_2), .ticker(n_bit_control_1_ticker), .comparison_input(comparator_1_eq),
    .done(counter_1_carry));
  Counter #(.width(4), .max('h8)) counter_1 (
    .count(n_bit_control_1_ticker), .carry(counter_1_carry), .clk(clock_1_out), .clr(n_bit_control_1_clr_2));  // open: load, D, Q
  seven_segment_controller seven_segment_controller_1 (
    .g(seven_segment_controller_1_g), .f(seven_segment_controller_1_f), .b(seven_segment_controller_1_b),
    .a(seven_segment_controller_1_a), .c(seven_segment_controller_1_c), .d(seven_segment_controller_1_d),
    .e(seven_segment_controller_1_e), .in_1({2'b00, double_dabble_2_1_result[9:8]}));
  _7_Segment_Display #(.active("false")) u_7_segment_display_1 (
    .g(seven_segment_controller_1_g), .f(seven_segment_controller_1_f), .a(seven_segment_controller_1_a),
    .b(seven_segment_controller_1_b), .e(seven_segment_controller_1_e), .d(seven_segment_controller_1_d),
    .c(seven_segment_controller_1_c), .dp(1'b1));
  Multiplexer #(.width(8), .enable("false")) multiplexer_1 (
    .in0(shift_register_1_q0), .in1(in_2), .out(multiplexer_1_out), .sel(n_bit_control_1_change_in_input));
  Shift_Register shift_register_1 (
    .shift(n_bit_control_1_enable_2), .in(1'b0), .clk(n_bit_control_1_clk_2), .out(shift_register_1_out),
    .load(n_bit_control_1_load_2), .clr(n_bit_control_1_clr_2), .d0(multiplexer_1_out[0]),
    .q0(shift_register_1_q0[0]), .d1(multiplexer_1_out[1]), .q1(shift_register_1_q0[1]),
    .d2(multiplexer_1_out[2]), .q2(shift_register_1_q0[2]), .d3(multiplexer_1_out[3]),
    .q3(shift_register_1_q0[3]), .d4(multiplexer_1_out[4]), .q4(shift_register_1_q0[4]),
    .d5(multiplexer_1_out[5]), .q5(shift_register_1_q0[5]), .d6(multiplexer_1_out[6]),
    .q6(shift_register_1_q0[6]), .d7(multiplexer_1_out[7]), .q7(shift_register_1_q0[7]));
  seven_segment_controller seven_segment_controller_2 (
    .g(seven_segment_controller_2_g), .f(seven_segment_controller_2_f), .b(seven_segment_controller_2_b),
    .a(seven_segment_controller_2_a), .c(seven_segment_controller_2_c), .d(seven_segment_controller_2_d),
    .e(seven_segment_controller_2_e), .in_1(double_dabble_2_1_result[7:4]));
  _7_Segment_Display #(.active("false")) u_7_segment_display_2 (
    .g(seven_segment_controller_2_g), .f(seven_segment_controller_2_f), .a(seven_segment_controller_2_a),
    .b(seven_segment_controller_2_b), .e(seven_segment_controller_2_e), .d(seven_segment_controller_2_d),
    .c(seven_segment_controller_2_c), .dp(1'b1));
  n_bit_double_dabble n_bit_double_dabble_1 ();  // open: greater_than_three_in_1, greater_than_three_out_1, Load, enable, clock, clear, greater_than_three_in_2, greater_than_three_out_2, Shift_out, result, shift_in, Load_2, enable_2, clock_2, clear_2
  n_bit_double_dabble n_bit_double_dabble_2 (
    .greater_than_three_in_1(1'b0),
    .greater_than_three_out_1(n_bit_double_dabble_2_greater_than_three_out_1), .Load(n_bit_control_1_load),
    .enable(n_bit_control_1_enable), .clock(n_bit_control_1_clk), .clear(n_bit_control_1_clr),
    .greater_than_three_in_2(n_bit_double_dabble_3_greater_than_three_out_1),
    .greater_than_three_out_2(n_bit_double_dabble_2_greater_than_three_out_2),
    .Shift_out(n_bit_double_dabble_2_shift_out), .result(n_bit_double_dabble_2_result),
    .shift_in(shift_register_1_out), .Load_2(n_bit_double_dabble_2_load_2),
    .enable_2(n_bit_double_dabble_2_enable_2), .clock_2(n_bit_double_dabble_2_clock_2),
    .clear_2(n_bit_double_dabble_2_clear_2));
  seven_segment_controller seven_segment_controller_3 (
    .g(seven_segment_controller_3_g), .f(seven_segment_controller_3_f), .b(seven_segment_controller_3_b),
    .a(seven_segment_controller_3_a), .c(seven_segment_controller_3_c), .d(seven_segment_controller_3_d),
    .e(seven_segment_controller_3_e), .in_1(n_bit_double_dabble_2_result));
  _7_Segment_Display #(.active("false")) u_7_segment_display_3 (
    .g(seven_segment_controller_3_g), .f(seven_segment_controller_3_f), .a(seven_segment_controller_3_a),
    .b(seven_segment_controller_3_b), .e(seven_segment_controller_3_e), .d(seven_segment_controller_3_d),
    .c(seven_segment_controller_3_c));  // open: dp
  seven_segment_controller seven_segment_controller_4 (
    .g(seven_segment_controller_4_g), .f(seven_segment_controller_4_f), .b(seven_segment_controller_4_b),
    .a(seven_segment_controller_4_a), .c(seven_segment_controller_4_c), .d(seven_segment_controller_4_d),
    .e(seven_segment_controller_4_e), .in_1(double_dabble_2_1_result[3:0]));
  _7_Segment_Display #(.active("false")) u_7_segment_display_4 (
    .g(seven_segment_controller_4_g), .f(seven_segment_controller_4_f), .a(seven_segment_controller_4_a),
    .b(seven_segment_controller_4_b), .e(seven_segment_controller_4_e), .d(seven_segment_controller_4_d),
    .c(seven_segment_controller_4_c), .dp(1'b1));
  n_bit_double_dabble n_bit_double_dabble_3 (
    .greater_than_three_in_1(n_bit_double_dabble_2_greater_than_three_out_2),
    .greater_than_three_out_1(n_bit_double_dabble_3_greater_than_three_out_1),
    .Load(n_bit_double_dabble_2_load_2), .enable(n_bit_double_dabble_2_enable_2),
    .clock(n_bit_double_dabble_2_clock_2), .clear(n_bit_double_dabble_2_clear_2),
    .greater_than_three_in_2(n_bit_double_dabble_4_greater_than_three_out_1),
    .greater_than_three_out_2(n_bit_double_dabble_3_greater_than_three_out_2),
    .Shift_out(n_bit_double_dabble_3_shift_out), .result(n_bit_double_dabble_3_result),
    .shift_in(n_bit_double_dabble_2_shift_out), .Load_2(n_bit_double_dabble_3_load_2),
    .enable_2(n_bit_double_dabble_3_enable_2), .clock_2(n_bit_double_dabble_3_clock_2),
    .clear_2(n_bit_double_dabble_3_clear_2));
  seven_segment_controller seven_segment_controller_5 (
    .g(seven_segment_controller_5_g), .f(seven_segment_controller_5_f), .b(seven_segment_controller_5_b),
    .a(seven_segment_controller_5_a), .c(seven_segment_controller_5_c), .d(seven_segment_controller_5_d),
    .e(seven_segment_controller_5_e), .in_1(n_bit_double_dabble_3_result));
  n_bit_double_dabble n_bit_double_dabble_4 (
    .greater_than_three_in_1(n_bit_double_dabble_3_greater_than_three_out_2),
    .greater_than_three_out_1(n_bit_double_dabble_4_greater_than_three_out_1),
    .Load(n_bit_double_dabble_3_load_2), .enable(n_bit_double_dabble_3_enable_2),
    .clock(n_bit_double_dabble_3_clock_2), .clear(n_bit_double_dabble_3_clear_2),
    .greater_than_three_in_2(1'b0), .result(n_bit_double_dabble_4_result),
    .shift_in(n_bit_double_dabble_3_shift_out));  // open: greater_than_three_out_2, Shift_out, Load_2, enable_2, clock_2, clear_2
  seven_segment_controller seven_segment_controller_6 (
    .g(seven_segment_controller_6_g), .f(seven_segment_controller_6_f), .b(seven_segment_controller_6_b),
    .a(seven_segment_controller_6_a), .c(seven_segment_controller_6_c), .d(seven_segment_controller_6_d),
    .e(seven_segment_controller_6_e), .in_1(n_bit_double_dabble_4_result));
  _7_Segment_Display #(.active("false")) u_7_segment_display_5 (
    .g(seven_segment_controller_5_g), .f(seven_segment_controller_5_f), .a(seven_segment_controller_5_a),
    .b(seven_segment_controller_5_b), .e(seven_segment_controller_5_e), .d(seven_segment_controller_5_d),
    .c(seven_segment_controller_5_c));  // open: dp
  _7_Segment_Display #(.active("false")) u_7_segment_display_6 (
    .g(seven_segment_controller_6_g), .f(seven_segment_controller_6_f), .a(seven_segment_controller_6_a),
    .b(seven_segment_controller_6_b), .e(seven_segment_controller_6_e), .d(seven_segment_controller_6_d),
    .c(seven_segment_controller_6_c));  // open: dp

  // Notes on the sheet:
  //   WIP, on a n-bit Double Dabble implementation below
endmodule

module double_dabble (
  input  [7:0] \input ,
  input  clock,
  output [9:0] result,
  output done
);

  wire and_1_out, and_2_out, and_3_out, and_4_out, and_5_out, and_6_out, and_7_out, and_8_out, and_9_out,
       and_10_out, and_12_out, and_13_out, and_14_out, and_15_out, and_16_out, and_17_out, and_18_out,
       counter_1_carry, n8_bit_comparator_1_a_b_2, nand_1_out, nand_2_out, nand_3_out, nor_1_out, not_1_out,
       not_2_out, not_3_out, not_4_out, not_5_out, not_6_out, not_7_out, not_8_out, not_9_out, not_10_out,
       not_11_out, not_12_out, not_13_out, not_14_out, or_1_out, or_2_out, or_3_out, or_4_out, or_5_out,
       or_6_out, or_7_out, or_8_out, or_9_out, or_10_out, register_2_q, register_3_q, xor_1_out, xor_2_out,
       xor_3_out;
  wire [3:0] n4_bit_lcu_adder_1_out_4, n4_bit_lcu_adder_2_out_4, n4_bit_mux_1_out_4, n4_bit_mux_2_out_4,
       n4_bit_mux_3_out_4, n4_bit_mux_4_out_4, n4_bit_mux_5_out_4;
  wire [7:0] n8_bit_mux_1_out_4, register_1_q, shift_register_1_q0;

  _8_bit_comparator u_8_bit_comparator_1 (
    .a(\input ), .b(register_1_q), .a_b_2(n8_bit_comparator_1_a_b_2));  // open: A_B, A_B_3
  Register register_1 (.D(\input ), .en(not_1_out), .Q(register_1_q), .clk(clock));  // open: clr
  not not_1 (not_1_out, n8_bit_comparator_1_a_b_2);
  Register #(.width(1)) register_2 (
    .D(nand_1_out), .en(n8_bit_comparator_1_a_b_2), .Q(register_2_q), .clk(and_2_out), .clr(not_4_out));
  not not_2 (not_2_out, register_2_q);
  nand nand_1 (nand_1_out, and_2_out, and_1_out);
  and and_1 (and_1_out, n8_bit_comparator_1_a_b_2, or_1_out);
  or or_1 (or_1_out, not_3_out, register_2_q);
  not not_3 (not_3_out, done);
  not not_4 (not_4_out, n8_bit_comparator_1_a_b_2);
  and and_2 (and_2_out, clock, not_5_out);
  not not_5 (not_5_out, done);
  and and_3 (and_3_out, or_10_out, not_6_out);
  not not_6 (not_6_out, and_2_out);
  and and_4 (and_4_out, not_6_out, or_9_out);
  nor nor_1 (nor_1_out, or_9_out, or_10_out);
  xor xor_1 (xor_1_out, nor_1_out, done);
  or or_2 (or_2_out, xor_1_out, register_3_q);
  nand nand_2 (nand_2_out, and_2_out, or_2_out);
  nand nand_3 (nand_3_out, nand_2_out, or_5_out);
  and and_5 (and_5_out, register_2_q, n8_bit_comparator_1_a_b_2);
  or or_3 (or_3_out, register_3_q, nand_3_out);
  and and_6 (and_6_out, and_5_out, or_3_out);
  Register #(.width(1)) register_3 (.D(xor_2_out), .en(or_4_out), .Q(register_3_q), .clk(and_2_out), .clr(not_4_out));
  xor xor_2 (xor_2_out, or_2_out, or_4_out);
  or or_4 (or_4_out, and_3_out, and_4_out);
  Shift_Register #(.length(18)) shift_register_1 (
    .shift(or_2_out), .in(1'b0), .clk(and_2_out), .load(or_6_out), .clr(not_4_out),
    .d0(n8_bit_mux_1_out_4[0]), .q0(shift_register_1_q0[0]), .d1(n8_bit_mux_1_out_4[1]),
    .q1(shift_register_1_q0[1]), .d2(n8_bit_mux_1_out_4[2]), .q2(shift_register_1_q0[2]),
    .d3(n8_bit_mux_1_out_4[3]), .q3(shift_register_1_q0[3]), .d4(n8_bit_mux_1_out_4[4]),
    .q4(shift_register_1_q0[4]), .d5(n8_bit_mux_1_out_4[5]), .q5(shift_register_1_q0[5]),
    .d6(n8_bit_mux_1_out_4[6]), .q6(shift_register_1_q0[6]), .d7(n8_bit_mux_1_out_4[7]),
    .q7(shift_register_1_q0[7]), .d8(n4_bit_mux_1_out_4[0]), .q8(result[0]), .d9(n4_bit_mux_1_out_4[1]),
    .q9(result[1]), .d10(n4_bit_mux_1_out_4[2]), .q10(result[2]), .d11(n4_bit_mux_1_out_4[3]),
    .q11(result[3]), .d12(n4_bit_mux_3_out_4[0]), .q12(result[4]), .d13(n4_bit_mux_3_out_4[1]),
    .q13(result[5]), .d14(n4_bit_mux_3_out_4[2]), .q14(result[6]), .d15(n4_bit_mux_3_out_4[3]),
    .q15(result[7]), .d16(n4_bit_mux_5_out_4[0]), .q16(result[8]), .d17(n4_bit_mux_5_out_4[1]),
    .q17(result[9]));  // open: out
  or or_5 (or_5_out, not_2_out, or_10_out, or_9_out);
  not not_7 (not_7_out, shift_register_1_q0[4]);
  not not_8 (not_8_out, shift_register_1_q0[3]);
  not not_9 (not_9_out, shift_register_1_q0[2]);
  and and_7 (and_7_out, not_8_out, and_14_out);
  Counter #(.width(4), .max('h8)) counter_1 (
    .count(and_6_out), .carry(counter_1_carry), .clk(and_2_out), .clr(not_4_out));  // open: load, D, Q
  and and_8 (and_8_out, not_9_out, and_7_out);
  not not_10 (not_10_out, shift_register_1_q0[1]);
  not not_11 (not_11_out, shift_register_1_q0[0]);
  and and_9 (and_9_out, not_10_out, and_8_out);
  and and_10 (and_10_out, not_11_out, and_9_out);
  and and_11 (done, counter_1_carry, and_10_out);
  or or_6 (or_6_out, not_2_out, xor_3_out);
  _8_bit_Mux u_8_bit_mux_1 (.in_1(\input ), .in_2(shift_register_1_q0), .in_3(not_2_out), .out_4(n8_bit_mux_1_out_4));
  not not_12 (not_12_out, shift_register_1_q0[7]);
  not not_13 (not_13_out, shift_register_1_q0[6]);
  and and_12 (and_12_out, not_13_out, not_12_out);
  not not_14 (not_14_out, shift_register_1_q0[5]);
  and and_13 (and_13_out, not_14_out, and_12_out);
  and and_14 (and_14_out, not_7_out, and_13_out);
  xor xor_3 (xor_3_out, or_4_out, register_3_q);
  or or_7 (or_7_out, or_10_out, or_9_out);
  _4_bit_Mux u_4_bit_mux_1 (.out_4(n4_bit_mux_1_out_4), .in_1(n4_bit_mux_2_out_4), .in_2(4'b0000), .select(or_7_out));
  _4_bit_Mux u_4_bit_mux_2 (
    .out_4(n4_bit_mux_2_out_4), .in_1(n4_bit_lcu_adder_1_out_4), .in_2(result[3:0]), .select(or_9_out));
  or or_8 (or_8_out, or_9_out, or_10_out);
  _4_bit_Mux u_4_bit_mux_3 (.out_4(n4_bit_mux_3_out_4), .in_1(n4_bit_mux_4_out_4), .in_2(4'b0000), .select(or_8_out));
  _4_bit_Mux u_4_bit_mux_4 (
    .out_4(n4_bit_mux_4_out_4), .in_1(n4_bit_lcu_adder_2_out_4), .in_2(result[7:4]), .select(or_10_out));
  and and_15 (and_15_out, result[0], result[2]);
  or or_9 (or_9_out, result[3], and_15_out, and_17_out);
  and and_16 (and_16_out, result[4], result[6]);
  or or_10 (or_10_out, result[7], and_16_out, and_18_out);
  _4_bit_Mux u_4_bit_mux_5 (
    .out_4(n4_bit_mux_5_out_4), .in_1(4'b0000), .in_2({2'b00, result[9:8]}), .select(not_2_out));
  and and_17 (and_17_out, result[2], result[1]);
  and and_18 (and_18_out, result[6], result[5]);
  _4_bit_LCU_adder u_4_bit_lcu_adder_1 (
    .in_1(4'b0011), .in_2(result[3:0]), .cin(1'b0), .out_4(n4_bit_lcu_adder_1_out_4));  // open: cout
  _4_bit_LCU_adder u_4_bit_lcu_adder_2 (
    .in_1(4'b0011), .in_2(result[7:4]), .cin(1'b0), .out_4(n4_bit_lcu_adder_2_out_4));  // open: cout
endmodule

module comparator (
  input  [7:0] B,
  input  [7:0] A,
  output A_B
);

  wire nand_1_out, nand_2_out, nor_1_out, nor_2_out, nor_4_out, nor_5_out, xor_1_out, xor_2_out, xor_3_out,
       xor_4_out, xor_5_out, xor_6_out, xor_7_out, xor_8_out;

  xor xor_1 (xor_1_out, B[0], A[0]);
  xor xor_2 (xor_2_out, B[1], A[1]);
  xor xor_3 (xor_3_out, B[2], A[2]);
  xor xor_4 (xor_4_out, B[3], A[3]);
  xor xor_5 (xor_5_out, B[4], A[4]);
  xor xor_6 (xor_6_out, B[5], A[5]);
  xor xor_7 (xor_7_out, B[6], A[6]);
  xor xor_8 (xor_8_out, B[7], A[7]);
  nor nor_1 (nor_1_out, xor_1_out, xor_2_out);
  nand nand_1 (nand_1_out, nor_1_out, nor_2_out);
  nor nor_2 (nor_2_out, xor_3_out, xor_4_out);
  nor nor_3 (A_B, nand_1_out, nand_2_out);
  nor nor_4 (nor_4_out, xor_5_out, xor_6_out);
  nand nand_2 (nand_2_out, nor_4_out, nor_5_out);
  nor nor_5 (nor_5_out, xor_7_out, xor_8_out);
endmodule

module greater_than_3_comp (
  input  [3:0] B,
  output out_2
);

  or or_1 (out_2, B[2], B[3]);
endmodule

module seven_segment_controller (
  input  [3:0] in_1,
  output g,
  output f,
  output b,
  output a,
  output c,
  output d,
  output e
);

  wire nand_1_out, nand_2_out, nand_3_out, nand_4_out, nand_5_out, nand_6_out, nand_7_out, nand_8_out,
       nand_9_out, nand_10_out, nand_11_out, nand_12_out, nand_13_out, not_1_out, not_2_out, not_3_out,
       not_4_out;

  not not_1 (not_1_out, in_1[3]);
  not not_2 (not_2_out, in_1[2]);
  not not_3 (not_3_out, in_1[1]);
  not not_4 (not_4_out, in_1[0]);
  nand nand_1 (nand_1_out, in_1[0], in_1[1], in_1[2]);
  nand nand_2 (nand_2_out, not_3_out, not_2_out, not_1_out);
  nand nand_3 (nand_3_out, in_1[0], not_2_out, not_1_out);
  nand nand_4 (nand_4_out, in_1[1], not_2_out);
  nand nand_5 (nand_5_out, in_1[1], in_1[0]);
  nand nand_6 (nand_6_out, in_1[2], in_1[1], not_4_out);
  nand nand_7 (nand_7_out, in_1[2], not_3_out, in_1[0]);
  nand nand_8 (nand_8_out, in_1[2], not_3_out, not_4_out);
  nand nand_9 (nand_9_out, not_1_out, not_2_out, not_3_out, in_1[0]);
  nand nand_10 (nand_10_out, in_1[0], not_2_out, not_3_out, in_1[0]);
  nand nand_11 (nand_11_out, in_1[2], not_3_out, not_4_out);
  nand nand_12 (nand_12_out, in_1[2], in_1[1], in_1[0]);
  nand nand_13 (nand_13_out, in_1[2], not_3_out);
  nand u_g (g, nand_1_out, nand_2_out);
  nand u_f (f, nand_3_out, nand_4_out, nand_5_out);
  nand u_b (b, nand_6_out, nand_7_out);
  nand u_a (a, nand_8_out, nand_9_out);
  nor u_c (c, in_1[2], not_3_out, in_1[0]);
  nand u_d (d, nand_10_out, nand_11_out, nand_12_out);
  nand u_e (e, not_4_out, nand_13_out);
endmodule

module _2_bit_comparator (
  input  [1:0] A,
  input  [1:0] B,
  output A_B,
  output A_B_2,
  output A_B_3
);

  wire and_1_out, and_2_out, and_3_out, and_4_out, and_5_out, and_6_out, not_1_out, not_2_out, not_3_out,
       not_4_out, not_5_out, not_6_out, not_7_out, not_8_out;

  not not_1 (not_1_out, B[1]);
  not not_2 (not_2_out, B[1]);
  not not_3 (not_3_out, B[0]);
  not not_4 (not_4_out, B[0]);
  not not_5 (not_5_out, A[1]);
  not not_6 (not_6_out, A[0]);
  not not_7 (not_7_out, A[0]);
  not not_8 (not_8_out, A[1]);
  and and_1 (and_1_out, A[1], not_1_out);
  or or_1 (A_B, and_1_out, and_2_out, and_3_out);
  and and_2 (and_2_out, A[0], not_2_out, not_3_out);
  and and_3 (and_3_out, A[0], A[1], not_4_out);
  and and_4 (and_4_out, not_5_out, B[1]);
  and and_5 (and_5_out, not_6_out, B[1], B[0]);
  or or_2 (A_B_3, and_4_out, and_5_out, and_6_out);
  and and_6 (and_6_out, not_7_out, not_8_out, B[0]);
  nor nor_1 (A_B_2, A_B, A_B_3);
endmodule

module _4_bit_comparator (
  input  [3:0] a,
  input  [3:0] b,
  output A_B,
  output a_b_2,
  output A_B_3
);

  wire [0:0] n2_bit_comparator_1_a_b, n2_bit_comparator_1_a_b_3, n2_bit_comparator_2_a_b,
       n2_bit_comparator_2_a_b_3;

  _2_bit_comparator u_2_bit_comparator_1 (
    .A(a[1:0]), .B(b[1:0]), .A_B(n2_bit_comparator_1_a_b[0]), .A_B_3(n2_bit_comparator_1_a_b_3[0]));  // open: A_B_2
  _2_bit_comparator u_2_bit_comparator_2 (
    .A({a[2], n2_bit_comparator_1_a_b[0]}), .B({b[2], n2_bit_comparator_1_a_b_3[0]}),
    .A_B(n2_bit_comparator_2_a_b[0]), .A_B_3(n2_bit_comparator_2_a_b_3[0]));  // open: A_B_2
  _2_bit_comparator u_2_bit_comparator_3 (
    .A({a[3], n2_bit_comparator_2_a_b[0]}), .B({b[3], n2_bit_comparator_2_a_b_3[0]}), .A_B(A_B),
    .A_B_2(a_b_2), .A_B_3(A_B_3));
endmodule

module _8_bit_comparator (
  input  [7:0] a,
  input  [7:0] b,
  output A_B,
  output a_b_2,
  output A_B_3
);

  wire [0:0] n4_bit_comparator_1_a_b, n4_bit_comparator_1_a_b_3, n4_bit_comparator_2_a_b,
       n4_bit_comparator_2_a_b_3;

  _4_bit_comparator u_4_bit_comparator_1 (
    .a(a[3:0]), .b(b[3:0]), .A_B(n4_bit_comparator_1_a_b[0]), .A_B_3(n4_bit_comparator_1_a_b_3[0]));  // open: a_b_2
  _4_bit_comparator u_4_bit_comparator_2 (
    .a({a[6:4], n4_bit_comparator_1_a_b[0]}), .b({b[6:4], n4_bit_comparator_1_a_b_3[0]}),
    .A_B(n4_bit_comparator_2_a_b[0]), .A_B_3(n4_bit_comparator_2_a_b_3[0]));  // open: a_b_2
  _2_bit_comparator u_2_bit_comparator_1 (
    .A({a[7], n4_bit_comparator_2_a_b[0]}), .B({b[7], n4_bit_comparator_2_a_b_3[0]}), .A_B(A_B),
    .A_B_2(a_b_2), .A_B_3(A_B_3));
endmodule

module flip_flop (
  input  set,
  input  D,
  input  reset,
  output q,
  output q_prime
);

  Clock clk ();  // open: out
endmodule

module double_dabble__2 (
  input  [7:0] \input ,
  input  clock,
  output done,
  output [9:0] result
);

  wire and_1_out, and_2_out, and_3_out, and_4_out, and_5_out, and_6_out, and_7_out, and_8_out, and_9_out,
       comparator_1_a_b, nand_1_out, nand_2_out, nand_3_out, nor_1_out, not_1_out, not_2_out, not_3_out,
       not_4_out, not_7_out, or_1_out, or_2_out, or_3_out, or_4_out, or_5_out, or_6_out, or_7_out, or_8_out,
       or_9_out, or_10_out, register_2_q, register_3_q, transmission_1_p1, transmission_1_p2,
       transmission_1_p4, xor_1_out, xor_2_out, xor_3_out;
  wire [3:0] n4_bit_lcu_adder_1_out_4, n4_bit_lcu_adder_2_out_4, n4_bit_mux_1_out_4, n4_bit_mux_2_out_4,
       n4_bit_mux_3_out_4, n4_bit_mux_4_out_4, n4_bit_mux_5_out_4;
  wire [7:0] n8_bit_mux_1_out_4, register_1_q, shift_register_1_q0;

  comparator comparator_1 (.B(\input ), .A(register_1_q), .A_B(comparator_1_a_b));
  Register register_1 (.D(\input ), .en(not_1_out), .Q(register_1_q), .clk(clock));  // open: clr
  not not_1 (not_1_out, comparator_1_a_b);
  Register #(.width(1)) register_2 (
    .D(nand_1_out), .en(comparator_1_a_b), .Q(register_2_q), .clk(transmission_1_p2), .clr(not_4_out));
  not not_2 (not_2_out, register_2_q);
  nand nand_1 (nand_1_out, transmission_1_p2, and_1_out);
  and and_1 (and_1_out, comparator_1_a_b, or_1_out);
  or or_1 (or_1_out, not_3_out, register_2_q);
  not not_3 (not_3_out, done);
  not not_4 (not_4_out, comparator_1_a_b);
  // Transmission_Gate transmission_1: pin names not known; wires that end beside it: transmission_1_p1, transmission_1_p2, 1'b0, transmission_1_p4
  // Transmission_Gate transmission_2: pin names not known; wires that end beside it: transmission_1_p4, transmission_1_p2, clock
  not not_5 (transmission_1_p1, done);
  not not_6 (transmission_1_p4, transmission_1_p1);
  and and_2 (and_2_out, or_10_out, not_7_out);
  not not_7 (not_7_out, transmission_1_p2);
  and and_3 (and_3_out, not_7_out, or_9_out);
  nor nor_1 (nor_1_out, or_9_out, or_10_out);
  xor xor_1 (xor_1_out, nor_1_out, done);
  or or_2 (or_2_out, xor_1_out, register_3_q);
  nand nand_2 (nand_2_out, transmission_1_p2, or_2_out);
  Register #(.width(1)) register_3 (
    .D(xor_2_out), .en(or_3_out), .Q(register_3_q), .clk(transmission_1_p2), .clr(not_4_out));
  xor xor_2 (xor_2_out, or_2_out, or_3_out);
  or or_3 (or_3_out, and_2_out, and_3_out);
  Shift_Register #(.length(18)) shift_register_1 (
    .shift(or_2_out), .in(1'b0), .clk(transmission_1_p2), .load(or_5_out), .clr(not_4_out),
    .d0(n8_bit_mux_1_out_4[0]), .q0(shift_register_1_q0[0]), .d1(n8_bit_mux_1_out_4[1]),
    .q1(shift_register_1_q0[1]), .d2(n8_bit_mux_1_out_4[2]), .q2(shift_register_1_q0[2]),
    .d3(n8_bit_mux_1_out_4[3]), .q3(shift_register_1_q0[3]), .d4(n8_bit_mux_1_out_4[4]),
    .q4(shift_register_1_q0[4]), .d5(n8_bit_mux_1_out_4[5]), .q5(shift_register_1_q0[5]),
    .d6(n8_bit_mux_1_out_4[6]), .q6(shift_register_1_q0[6]), .d7(n8_bit_mux_1_out_4[7]),
    .q7(shift_register_1_q0[7]), .d8(n4_bit_mux_1_out_4[0]), .q8(result[0]), .d9(n4_bit_mux_1_out_4[1]),
    .q9(result[1]), .d10(n4_bit_mux_1_out_4[2]), .q10(result[2]), .d11(n4_bit_mux_1_out_4[3]),
    .q11(result[3]), .d12(n4_bit_mux_3_out_4[0]), .q12(result[4]), .d13(n4_bit_mux_3_out_4[1]),
    .q13(result[5]), .d14(n4_bit_mux_3_out_4[2]), .q14(result[6]), .d15(n4_bit_mux_3_out_4[3]),
    .q15(result[7]), .d16(n4_bit_mux_5_out_4[0]), .q16(result[8]), .d17(n4_bit_mux_5_out_4[1]),
    .q17(result[9]));  // open: out
  and and_4 (and_4_out, register_2_q, comparator_1_a_b);
  or or_4 (or_4_out, register_3_q, nand_3_out);
  and and_5 (and_5_out, and_4_out, or_4_out);
  or or_5 (or_5_out, not_2_out, xor_3_out);
  _8_bit_Mux u_8_bit_mux_1 (.in_1(\input ), .in_2(shift_register_1_q0), .in_3(not_2_out), .out_4(n8_bit_mux_1_out_4));
  or or_6 (or_6_out, not_2_out, or_10_out, or_9_out);
  nand nand_3 (nand_3_out, nand_2_out, or_6_out);
  Counter #(.width(4), .max('h8)) counter_1 (
    .count(and_5_out), .carry(done), .clk(transmission_1_p2), .clr(not_4_out));  // open: load, D, Q
  xor xor_3 (xor_3_out, or_3_out, register_3_q);
  or or_7 (or_7_out, or_10_out, or_9_out);
  _4_bit_Mux u_4_bit_mux_1 (.out_4(n4_bit_mux_1_out_4), .in_1(n4_bit_mux_2_out_4), .in_2(4'b0000), .select(or_7_out));
  _4_bit_Mux u_4_bit_mux_2 (
    .out_4(n4_bit_mux_2_out_4), .in_1(n4_bit_lcu_adder_1_out_4), .in_2(result[3:0]), .select(or_9_out));
  or or_8 (or_8_out, or_9_out, or_10_out);
  _4_bit_Mux u_4_bit_mux_3 (.out_4(n4_bit_mux_3_out_4), .in_1(n4_bit_mux_4_out_4), .in_2(4'b0000), .select(or_8_out));
  _4_bit_Mux u_4_bit_mux_4 (
    .out_4(n4_bit_mux_4_out_4), .in_1(n4_bit_lcu_adder_2_out_4), .in_2(result[7:4]), .select(or_10_out));
  and and_6 (and_6_out, result[0], result[2]);
  or or_9 (or_9_out, result[3], and_6_out, and_8_out);
  and and_7 (and_7_out, result[4], result[6]);
  or or_10 (or_10_out, result[7], and_7_out, and_9_out);
  _4_bit_Mux u_4_bit_mux_5 (
    .out_4(n4_bit_mux_5_out_4), .in_1(4'b0000), .in_2({2'b00, result[9:8]}), .select(not_2_out));
  and and_8 (and_8_out, result[2], result[1]);
  and and_9 (and_9_out, result[6], result[5]);
  _4_bit_LCU_adder u_4_bit_lcu_adder_1 (
    .in_1(4'b0011), .in_2(result[3:0]), .cin(1'b0), .out_4(n4_bit_lcu_adder_1_out_4));  // open: cout
  _4_bit_LCU_adder u_4_bit_lcu_adder_2 (
    .in_1(4'b0011), .in_2(result[7:4]), .cin(1'b0), .out_4(n4_bit_lcu_adder_2_out_4));  // open: cout
endmodule

module test (
  input  in_1,
  input  in_2,
  input  control
);

  wire controlled_buffer_1_out, not_1_out;

  assign controlled_buffer_1_out = control ? in_1 : 1'bz;  // Controlled_Buffer controlled_buffer_1
  assign controlled_buffer_1_out = not_1_out ? in_2 : 1'bz;  // Controlled_Buffer controlled_buffer_2
  not not_1 (not_1_out, control);
endmodule

module n_bit_double_dabble (
  input  greater_than_three_in_1,
  input  greater_than_three_in_2,
  input  Load,
  input  enable,
  input  shift_in,
  input  clock,
  input  clear,
  output greater_than_three_out_1,
  output greater_than_three_out_2,
  output Load_2,
  output enable_2,
  output Shift_out,
  output clock_2,
  output clear_2,
  output [3:0] result
);

  wire and_1_out, and_2_out, greater_than_three, or_1_out, register_1_q;
  wire [3:0] n4_bit_lcu_adder_1_out_4, n4_bit_mux_1_out_4, n4_bit_mux_2_out_4;

  Shift_Register #(.length(4)) shift_register_1 (
    .shift(enable), .in(shift_in), .clk(clock), .out(Shift_out), .load(Load), .clr(clear),
    .d0(n4_bit_mux_1_out_4[0]), .q0(result[3]), .d1(n4_bit_mux_1_out_4[1]), .q1(result[2]),
    .d2(n4_bit_mux_1_out_4[2]), .q2(result[1]), .d3(n4_bit_mux_1_out_4[3]), .q3(result[0]));
  or or_1 (or_1_out, greater_than_three_in_1, greater_than_three_in_2);
  Register #(.width(1)) register_1 (.D(or_1_out), .Q(register_1_q), .clk(clock), .clr(clear));  // open: en
  or or_2 (greater_than_three_out_1, register_1_q, greater_than_three);
  _4_bit_Mux u_4_bit_mux_1 (
    .out_4(n4_bit_mux_1_out_4), .in_1(n4_bit_mux_2_out_4), .in_2(4'b0000), .select(greater_than_three_out_1));
  and and_1 (and_1_out, result[1], result[2]);
  and and_2 (and_2_out, result[3], result[1]);
  or or_3 (greater_than_three, result[0], and_2_out, and_1_out);
  _4_bit_Mux u_4_bit_mux_2 (
    .out_4(n4_bit_mux_2_out_4), .in_1(n4_bit_lcu_adder_1_out_4),
    .in_2({result[0], result[1], result[2], result[3]}), .select(greater_than_three));
  _4_bit_LCU_adder u_4_bit_lcu_adder_1 (
    .in_1(4'b0011), .in_2({result[0], result[1], result[2], result[3]}), .cin(1'b0),
    .out_4(n4_bit_lcu_adder_1_out_4));  // open: cout

  assign clear_2 = clear;
  assign clock_2 = clock;
  assign enable_2 = enable;
  assign greater_than_three_out_2 = greater_than_three_out_1;
  assign Load_2 = Load;

  // Other names for the same wires on the sheet: clk = clock; clr = clear
endmodule

module seven (
  input  _0,
  input  _1,
  input  _2,
  input  _3,
  output g,
  output f,
  output b,
  output a,
  output c,
  output d,
  output e
);

  wire nand_1_out, nand_2_out, nand_3_out, nand_4_out, nand_5_out, nand_6_out, nand_7_out, nand_8_out,
       nand_9_out, nand_10_out, nand_11_out, nand_12_out, nand_13_out, not_1_out, not_2_out, not_3_out,
       not_4_out;

  not not_1 (not_1_out, _3);
  not not_2 (not_2_out, _2);
  not not_3 (not_3_out, _1);
  not not_4 (not_4_out, _0);
  nand nand_1 (nand_1_out, _0, _1, _2);
  nand nand_2 (nand_2_out, not_3_out, not_2_out, not_1_out);
  nand nand_3 (nand_3_out, _0, not_2_out, not_1_out);
  nand nand_4 (nand_4_out, _1, not_2_out);
  nand nand_5 (nand_5_out, _1, _0);
  nand nand_6 (nand_6_out, _2, _1, not_4_out);
  nand nand_7 (nand_7_out, _2, not_3_out, _0);
  nand nand_8 (nand_8_out, _2, not_3_out, not_4_out);
  nand nand_9 (nand_9_out, not_1_out, not_2_out, not_3_out, _0);
  nand nand_10 (nand_10_out, _0, not_2_out, not_3_out, _0);
  nand nand_11 (nand_11_out, _2, not_3_out, not_4_out);
  nand nand_12 (nand_12_out, _2, _1, _0);
  nand nand_13 (nand_13_out, _2, not_3_out);
  nand u_g (g, nand_1_out, nand_2_out);
  nand u_f (f, nand_3_out, nand_4_out, nand_5_out);
  nand u_b (b, nand_6_out, nand_7_out);
  nand u_a (a, nand_8_out, nand_9_out);
  nor u_c (c, _2, not_3_out, _0);
  nand u_d (d, nand_10_out, nand_11_out, nand_12_out);
  nand u_e (e, not_4_out, nand_13_out);
endmodule

module seven2 (
  input  h,
  input  x2,
  input  x3,
  input  x4,
  output g,
  output f,
  output b,
  output a,
  output c,
  output d,
  output e
);

  wire and_1_out, and_2_out, and_3_out, and_4_out, and_5_out, and_6_out, and_7_out, and_8_out, and_9_out,
       and_10_out, and_11_out, and_12_out, and_13_out, and_14_out, nand_1_out, nand_2_out, nand_3_out,
       nand_4_out, nand_5_out, nand_6_out, nand_7_out, nand_8_out, nand_9_out, nand_10_out, nand_11_out,
       nand_14_out, nand_17_out, not_1_out, not_2_out, not_3_out, not_4_out, not_5_out, not_6_out, not_7_out,
       not_8_out, not_9_out, not_10_out, not_11_out, not_12_out, not_13_out, not_14_out, not_15_out,
       not_16_out, not_17_out, not_18_out, not_19_out, not_20_out, or_1_out;

  not not_1 (not_1_out, x2);
  not not_2 (not_2_out, x3);
  not not_3 (not_3_out, x3);
  not not_4 (not_4_out, x2);
  not not_5 (not_5_out, x2);
  not not_6 (not_6_out, x4);
  not not_7 (not_7_out, x3);
  not not_8 (not_8_out, x2);
  not not_9 (not_9_out, x2);
  not not_10 (not_10_out, x3);
  not not_11 (not_11_out, x2);
  not not_12 (not_12_out, x2);
  not not_13 (not_13_out, x2);
  and and_1 (and_1_out, h, x2);
  and and_2 (and_2_out, not_1_out, not_2_out);
  not not_14 (not_14_out, x4);
  and and_3 (and_3_out, h, not_3_out);
  not not_15 (not_15_out, x4);
  not not_16 (not_16_out, x3);
  and and_4 (and_4_out, x3, x2);
  not not_17 (not_17_out, h);
  and and_5 (and_5_out, x3, not_4_out);
  and and_6 (and_6_out, x3, not_5_out);
  not not_18 (not_18_out, h);
  and and_7 (and_7_out, not_6_out, not_7_out);
  and and_8 (and_8_out, not_8_out, h);
  or or_1 (or_1_out, x3, not_9_out);
  and and_9 (and_9_out, h, not_10_out);
  and and_10 (and_10_out, not_11_out, h);
  and and_11 (and_11_out, x3, not_12_out);
  not not_19 (not_19_out, h);
  not not_20 (not_20_out, h);
  nand nand_1 (nand_1_out, x3, not_13_out);
  nand nand_2 (nand_2_out, and_1_out, x3);
  nand nand_3 (nand_3_out, and_2_out, not_14_out);
  nand nand_4 (nand_4_out, and_3_out, not_15_out);
  nand nand_5 (nand_5_out, x2, not_16_out);
  nand nand_6 (nand_6_out, and_4_out, not_17_out);
  nand nand_7 (nand_7_out, and_5_out, h);
  nand nand_8 (nand_8_out, and_6_out, not_18_out);
  nand nand_9 (nand_9_out, and_7_out, and_8_out);
  nor nor_1 (c, or_1_out, h);
  nand nand_10 (nand_10_out, and_9_out, and_10_out);
  nand nand_11 (nand_11_out, and_11_out, not_19_out);
  and and_12 (and_12_out, x3, x2);
  nand nand_12 (e, not_20_out, nand_1_out);
  nand nand_13 (g, nand_2_out, nand_3_out);
  and and_13 (and_13_out, nand_4_out, nand_5_out);
  nand nand_14 (nand_14_out, x2, h);
  nand nand_15 (b, nand_6_out, nand_7_out);
  nand nand_16 (a, nand_8_out, nand_9_out);
  and and_14 (and_14_out, nand_10_out, nand_11_out);
  nand nand_17 (nand_17_out, and_12_out, h);
  nand nand_18 (f, and_13_out, nand_14_out);
  nand nand_19 (d, and_14_out, nand_17_out);
endmodule

module n_bit_control (
  input  greaterthanthree,
  input  comparison_input,
  input  done,
  input  clock,
  output Load_2,
  output change_in_input,
  output Load,
  output Enable_2,
  output Enable,
  output clk_2,
  output clk,
  output clr_2,
  output clr,
  output ticker
);

  wire and_1_out, and_2_out, and_3_out, nand_1_out, nand_2_out, nand_3_out, not_1_out, not_3_out, not_7_out,
       not_8_out, or_1_out, or_3_out, or_5_out, register_1_q, register_2_q, transmission_1_p1,
       transmission_2_p1, xor_1_out, xor_2_out, xor_3_out;

  not not_1 (not_1_out, comparison_input);
  Register #(.width(1)) register_1 (.D(nand_1_out), .en(not_1_out), .Q(register_1_q), .clk(clk), .clr(clr));
  nand nand_1 (nand_1_out, clk, and_1_out);
  not not_2 (change_in_input, register_1_q);
  and and_1 (and_1_out, not_1_out, or_1_out);
  or or_1 (or_1_out, not_3_out, register_1_q);
  not not_3 (not_3_out, done);
  not not_4 (clr, not_1_out);
  // Transmission_Gate transmission_1: pin names not known; wires that end beside it: transmission_1_p1, clk, 1'b0
  // Transmission_Gate transmission_2: pin names not known; wires that end beside it: transmission_2_p1, transmission_2_p1, clk, clock
  not not_5 (transmission_1_p1, done);
  not not_6 (transmission_2_p1, transmission_1_p1);
  not not_7 (not_7_out, clk);
  and and_2 (and_2_out, not_7_out, greaterthanthree);
  not not_8 (not_8_out, greaterthanthree);
  xor xor_1 (xor_1_out, not_8_out, done);
  or or_2 (Enable, xor_1_out, register_2_q);
  nand nand_2 (nand_2_out, clk, Enable);
  xor xor_2 (xor_2_out, Enable, and_2_out);
  Register #(.width(1)) register_2 (.D(xor_2_out), .en(and_2_out), .Q(register_2_q), .clk(clk), .clr(clr));
  or or_3 (or_3_out, register_2_q, nand_3_out);
  and and_3 (and_3_out, register_1_q, not_1_out);
  and and_4 (ticker, and_3_out, or_3_out);
  xor xor_3 (xor_3_out, and_2_out, register_2_q);
  or or_4 (Load, change_in_input, xor_3_out);
  or or_5 (or_5_out, change_in_input, greaterthanthree);
  nand nand_3 (nand_3_out, nand_2_out, or_5_out);

  assign clk_2 = clk;
  assign clr_2 = clr;
  assign Enable_2 = Enable;
  assign Load_2 = Load;
endmodule
