// Logisim project CarrySelectAdder.circ as structural Verilog: 11 circuits, main circuit logic mux2
module logic_mux2 (
  input  sel,
  input  x0,
  input  x1,
  output y
);

  wire nand_1_out, nand_3_out, not_1_out;

  not not_1 (not_1_out, sel);
  nand nand_1 (nand_1_out, x0, not_1_out);
  nand nand_2 (y, nand_1_out, nand_3_out);
  nand nand_3 (nand_3_out, x1, sel);
endmodule

module transimision_mux2i (
  input  in0,
  input  in1,
  input  sel,
  output out_4
);

  wire not_1_out, transistor_1_out;

  Transistor transistor_1 (.in(in0), .out(transistor_1_out), .gate(sel));
  Transistor #(.\type ("n"), .gate("br")) transistor_2 (.in(in0), .out(transistor_1_out), .gate(not_1_out));
  not not_1 (not_1_out, sel);
  Transistor transistor_3 (.in(in1), .out(transistor_1_out), .gate(not_1_out));
  Transistor #(.\type ("n"), .gate("br")) transistor_4 (.in(in1), .out(transistor_1_out), .gate(sel));
  not not_2 (out_4, transistor_1_out);
endmodule

module _4_1MUxX_logic (
  input  x0,
  input  x1,
  input  x2,
  input  select_1,
  input  x3,
  input  select_0,
  output out_7
);

  wire logic_mux2_1_y, logic_mux2_2_y;

  logic_mux2 logic_mux2_1 (.x0(x0), .x1(x1), .y(logic_mux2_1_y), .sel(select_0));
  logic_mux2 logic_mux2_2 (.x0(x2), .x1(x3), .y(logic_mux2_2_y), .sel(select_0));
  logic_mux2 logic_mux2_3 (.x0(logic_mux2_1_y), .x1(logic_mux2_2_y), .y(out_7), .sel(select_1));
endmodule

module _4_1Mux_transmission (
  input  x0,
  input  x1,
  input  x2,
  input  select_1,
  input  x3,
  input  select_0,
  output out_7
);

  wire transimision_mux2i_1_out_4, transimision_mux2i_2_out_4;

  transimision_mux2i transimision_mux2i_1 (.in0(x0), .in1(x1), .sel(select_0), .out_4(transimision_mux2i_1_out_4));
  transimision_mux2i transimision_mux2i_2 (.in0(x2), .in1(x3), .sel(select_0), .out_4(transimision_mux2i_2_out_4));
  transimision_mux2i transimision_mux2i_3 (
    .in0(transimision_mux2i_1_out_4), .in1(transimision_mux2i_2_out_4), .sel(select_1), .out_4(out_7));
endmodule

module _8_bit_Carry_Select_Adder (
  input  [7:0] in_1,
  input  [7:0] in_2,
  input  cin,
  output cout,
  output [7:0] out_5
);

  wire n4_bit_adder_w_carry_out_1_out_4, n4_bit_adder_w_carry_out_2_out_4, n4_bit_adder_w_carry_out_3_out_4,
       transimision_mux2i_1_out_4;
  wire [3:0] n4_bit_adder_w_carry_out_2_out_5, n4_bit_adder_w_carry_out_3_out_5;

  _4_bit_adder_w_carry_out u_4_bit_adder_w_carry_out_1 (
    .in_1(in_2[3:0]), .in_2(in_1[3:0]), .in_3(cin), .out_4(n4_bit_adder_w_carry_out_1_out_4),
    .out_5(out_5[3:0]));
  _4_bit_adder_w_carry_out u_4_bit_adder_w_carry_out_2 (
    .in_1(in_2[7:4]), .in_2(in_1[7:4]), .in_3(1'b1), .out_4(n4_bit_adder_w_carry_out_2_out_4),
    .out_5(n4_bit_adder_w_carry_out_2_out_5));
  _4_bit_adder_w_carry_out u_4_bit_adder_w_carry_out_3 (
    .in_1(in_2[7:4]), .in_2(in_1[7:4]), .in_3(1'b0), .out_4(n4_bit_adder_w_carry_out_3_out_4),
    .out_5(n4_bit_adder_w_carry_out_3_out_5));
  _4_bit_Mux u_4_bit_mux_1 (
    .out_4(out_5[7:4]), .in_1(n4_bit_adder_w_carry_out_2_out_5), .in_2(n4_bit_adder_w_carry_out_3_out_5),
    .select(n4_bit_adder_w_carry_out_1_out_4));
  transimision_mux2i transimision_mux2i_1 (
    .in0(n4_bit_adder_w_carry_out_3_out_4), .in1(n4_bit_adder_w_carry_out_2_out_4),
    .sel(n4_bit_adder_w_carry_out_1_out_4), .out_4(transimision_mux2i_1_out_4));
  not not_1 (cout, transimision_mux2i_1_out_4);
endmodule

module _4_bit_Mux (
  input  [3:0] in_1,
  input  [3:0] in_2,
  input  select,
  output [3:0] out_4
);

  wire [3:0] transimision_mux2i_1_out_4;

  transimision_mux2i transimision_mux2i_1 (
    .in0(in_2[0]), .in1(in_1[0]), .sel(select), .out_4(transimision_mux2i_1_out_4[0]));
  transimision_mux2i transimision_mux2i_2 (
    .in0(in_2[1]), .in1(in_1[1]), .sel(select), .out_4(transimision_mux2i_1_out_4[1]));
  transimision_mux2i transimision_mux2i_3 (
    .in0(in_2[2]), .in1(in_1[2]), .sel(select), .out_4(transimision_mux2i_1_out_4[2]));
  transimision_mux2i transimision_mux2i_4 (
    .in0(in_2[3]), .in1(in_1[3]), .sel(select), .out_4(transimision_mux2i_1_out_4[3]));
  assign out_4 = ~transimision_mux2i_1_out_4;  // NOT_Gate not_1, 4 bits wide
endmodule

module _8_bit_Mux (
  input  [7:0] in_1,
  input  [7:0] in_2,
  input  in_3,
  output [7:0] out_4
);

  _4_bit_Mux u_4_bit_mux_1 (.out_4(out_4[3:0]), .in_1(in_1[3:0]), .in_2(in_2[3:0]), .select(in_3));
  _4_bit_Mux u_4_bit_mux_2 (.out_4(out_4[7:4]), .in_1(in_1[7:4]), .in_2(in_2[7:4]), .select(in_3));
endmodule

module _16_bit_Carry_Select_Adder (
  input  [15:0] in_1,
  input  [15:0] in_2,
  input  cin,
  output cout,
  output [15:0] out_5
);

  wire n8_bit_carry_select_adder_1_cout, n8_bit_carry_select_adder_2_cout, n8_bit_carry_select_adder_3_cout,
       transimision_mux2i_1_out_4;
  wire [7:0] n8_bit_carry_select_adder_2_out_5, n8_bit_carry_select_adder_3_out_5;

  _8_bit_Carry_Select_Adder u_8_bit_carry_select_adder_1 (
    .in_1(in_2[7:0]), .in_2(in_1[7:0]), .cin(cin), .cout(n8_bit_carry_select_adder_1_cout), .out_5(out_5[7:0]));
  _8_bit_Carry_Select_Adder u_8_bit_carry_select_adder_2 (
    .in_1(in_2[15:8]), .in_2(in_1[15:8]), .cin(1'b1), .cout(n8_bit_carry_select_adder_2_cout),
    .out_5(n8_bit_carry_select_adder_2_out_5));
  _8_bit_Carry_Select_Adder u_8_bit_carry_select_adder_3 (
    .in_1(in_2[15:8]), .in_2(in_1[15:8]), .cin(1'b0), .cout(n8_bit_carry_select_adder_3_cout),
    .out_5(n8_bit_carry_select_adder_3_out_5));
  _8_bit_Mux u_8_bit_mux_1 (
    .in_1(n8_bit_carry_select_adder_2_out_5), .in_2(n8_bit_carry_select_adder_3_out_5),
    .in_3(n8_bit_carry_select_adder_1_cout), .out_4(out_5[15:8]));
  transimision_mux2i transimision_mux2i_1 (
    .in0(n8_bit_carry_select_adder_3_cout), .in1(n8_bit_carry_select_adder_2_cout),
    .sel(n8_bit_carry_select_adder_1_cout), .out_4(transimision_mux2i_1_out_4));
  not not_1 (cout, transimision_mux2i_1_out_4);
endmodule

module _32_bit_Carry_Select_Adder (
  input  [31:0] in_1,
  input  [31:0] in_2,
  input  cin,
  output cout,
  output [31:0] out_5
);

  wire n16_bit_carry_select_adder_1_cout, n16_bit_carry_select_adder_2_cout,
       n16_bit_carry_select_adder_3_cout, transimision_mux2i_1_out_4;
  wire [15:0] n16_bit_carry_select_adder_2_out_5, n16_bit_carry_select_adder_3_out_5;

  _16_bit_Carry_Select_Adder u_16_bit_carry_select_adder_1 (
    .in_1(in_2[15:0]), .in_2(in_1[15:0]), .cin(cin), .cout(n16_bit_carry_select_adder_1_cout),
    .out_5(out_5[15:0]));
  _16_bit_Carry_Select_Adder u_16_bit_carry_select_adder_2 (
    .in_1(in_2[31:16]), .in_2(in_1[31:16]), .cin(1'b1), .cout(n16_bit_carry_select_adder_2_cout),
    .out_5(n16_bit_carry_select_adder_2_out_5));
  _16_bit_Mux u_16_bit_mux_1 (
    .in_1(n16_bit_carry_select_adder_2_out_5), .in_2(n16_bit_carry_select_adder_3_out_5),
    .in_3(n16_bit_carry_select_adder_1_cout), .out_4(out_5[31:16]));
  _16_bit_Carry_Select_Adder u_16_bit_carry_select_adder_3 (
    .in_1(in_2[31:16]), .in_2(in_1[31:16]), .cin(1'b0), .cout(n16_bit_carry_select_adder_3_cout),
    .out_5(n16_bit_carry_select_adder_3_out_5));
  transimision_mux2i transimision_mux2i_1 (
    .in0(n16_bit_carry_select_adder_3_cout), .in1(n16_bit_carry_select_adder_2_cout),
    .sel(n16_bit_carry_select_adder_1_cout), .out_4(transimision_mux2i_1_out_4));
  not not_1 (cout, transimision_mux2i_1_out_4);
endmodule

module _16_bit_Mux (
  input  [15:0] in_1,
  input  [15:0] in_2,
  input  in_3,
  output [15:0] out_4
);

  _8_bit_Mux u_8_bit_mux_1 (.in_1(in_1[7:0]), .in_2(in_2[7:0]), .in_3(in_3), .out_4(out_4[7:0]));
  _8_bit_Mux u_8_bit_mux_2 (.in_1(in_1[15:8]), .in_2(in_2[15:8]), .in_3(in_3), .out_4(out_4[15:8]));
endmodule

module subtract_or_add (
  input  [7:0] in_1,
  input  [7:0] in_2,
  input  mode,
  output cout,
  output [7:0] out_5
);

  wire n4_bit_adder_w_carry_out_1_out_4, n4_bit_adder_w_carry_out_2_out_4, n4_bit_adder_w_carry_out_3_out_4,
       transimision_mux2i_1_out_4;
  wire [3:0] n4_bit_adder_w_carry_out_2_out_5, n4_bit_adder_w_carry_out_3_out_5, undriven, undriven_2;

  _4_bit_adder_w_carry_out u_4_bit_adder_w_carry_out_1 (
    .in_1(in_2[3:0]), .in_2(undriven), .in_3(mode), .out_4(n4_bit_adder_w_carry_out_1_out_4),
    .out_5(out_5[3:0]));
  _4_bit_adder_w_carry_out u_4_bit_adder_w_carry_out_2 (
    .in_1(in_2[7:4]), .in_2(undriven_2), .in_3(1'b1), .out_4(n4_bit_adder_w_carry_out_2_out_4),
    .out_5(n4_bit_adder_w_carry_out_2_out_5));
  _4_bit_adder_w_carry_out u_4_bit_adder_w_carry_out_3 (
    .in_1(in_2[7:4]), .in_2(undriven_2), .in_3(1'b0), .out_4(n4_bit_adder_w_carry_out_3_out_4),
    .out_5(n4_bit_adder_w_carry_out_3_out_5));
  _4_bit_Mux u_4_bit_mux_1 (
    .out_4(out_5[7:4]), .in_1(n4_bit_adder_w_carry_out_2_out_5), .in_2(n4_bit_adder_w_carry_out_3_out_5),
    .select(n4_bit_adder_w_carry_out_1_out_4));
  transimision_mux2i transimision_mux2i_1 (
    .in0(n4_bit_adder_w_carry_out_3_out_4), .in1(n4_bit_adder_w_carry_out_2_out_4),
    .sel(n4_bit_adder_w_carry_out_1_out_4), .out_4(transimision_mux2i_1_out_4));
  _8_bit_Mux u_8_bit_mux_1 ();  // open: in_1, in_2, in_3, out_4
  not not_1 (cout, transimision_mux2i_1_out_4);
endmodule
