// Logisim project adder.circ as structural Verilog: 6 circuits, main circuit adder
module adder (
  input  a,
  input  b,
  input  carryin,
  output sum,
  output cout
);

  wire nand_1_out, nand_2_out, nand_3_out, nand_4_out, nand_5_out, nand_6_out, nand_8_out, nand_10_out,
       not_1_out, not_2_out, not_3_out, not_4_out;

  not not_1 (not_1_out, a);
  not not_2 (not_2_out, b);
  nand nand_1 (nand_1_out, b, not_1_out);
  nand nand_2 (nand_2_out, a, not_2_out);
  nand nand_3 (nand_3_out, nand_1_out, nand_2_out);
  nand nand_4 (nand_4_out, a, b);
  nand nand_5 (nand_5_out, b, carryin);
  nand nand_6 (nand_6_out, carryin, a);
  not not_3 (not_3_out, carryin);
  not not_4 (not_4_out, nand_3_out);
  nand nand_7 (cout, nand_4_out, nand_5_out, nand_6_out);
  nand nand_8 (nand_8_out, nand_3_out, not_3_out);
  nand nand_9 (sum, nand_8_out, nand_10_out);
  nand nand_10 (nand_10_out, carryin, not_4_out);
endmodule

module half_adder (
  input  in_1,
  input  in_2,
  output out_3,
  output out_4
);

  wire nand_1_out, nand_2_out, not_1_out, not_2_out;

  not not_1 (not_1_out, in_2);
  not not_2 (not_2_out, in_1);
  nand nand_1 (nand_1_out, in_1, not_1_out);
  nand nand_2 (nand_2_out, in_2, not_2_out);
  and and_1 (out_4, in_2, in_1);
  nand nand_3 (out_3, nand_1_out, nand_2_out);
endmodule

module _4_bit_adder (
  input  [3:0] in_1,
  input  [3:0] in_2,
  output out_3,
  output [3:0] out_4
);

  wire adder_1_cout, adder_2_cout, half_adder_1_out_4;

  half_adder half_adder_1 (.in_1(in_1[0]), .in_2(in_2[0]), .out_3(out_4[0]), .out_4(half_adder_1_out_4));
  adder adder_1 (.a(in_1[1]), .carryin(half_adder_1_out_4), .b(in_2[1]), .cout(adder_1_cout), .sum(out_4[1]));
  adder adder_2 (.a(in_1[2]), .carryin(adder_1_cout), .b(in_2[2]), .cout(adder_2_cout), .sum(out_4[2]));
  adder adder_3 (.a(in_2[3]), .carryin(adder_2_cout), .b(in_1[3]), .cout(out_3), .sum(out_4[3]));
endmodule

module _8_bit_adder (
  input  [7:0] in_1,
  input  [7:0] in_2,
  output [7:0] out_3
);

  wire n4_bit_adder_1_out_3;

  _4_bit_adder u_4_bit_adder_1 (.in_1(in_1[3:0]), .in_2(in_2[3:0]), .out_3(n4_bit_adder_1_out_3), .out_4(out_3[3:0]));
  _4_bit_adder_w_carry_out u_4_bit_adder_w_carry_out_1 (
    .in_1(in_1[7:4]), .in_2(in_2[7:4]), .in_3(n4_bit_adder_1_out_3), .out_5(out_3[7:4]));  // open: out_4
endmodule

module _4_bit_adder_w_carry_out (
  input  [3:0] in_1,
  input  [3:0] in_2,
  input  in_3,
  output out_4,
  output [3:0] out_5
);

  wire adder_1_cout, adder_2_cout, adder_3_cout;

  adder adder_1 (.a(in_1[0]), .carryin(in_3), .b(in_2[0]), .cout(adder_1_cout), .sum(out_5[0]));
  adder adder_2 (.a(in_1[1]), .carryin(adder_1_cout), .b(in_2[1]), .cout(adder_2_cout), .sum(out_5[1]));
  adder adder_3 (.a(in_1[2]), .carryin(adder_2_cout), .b(in_2[2]), .cout(adder_3_cout), .sum(out_5[2]));
  adder adder_4 (.a(in_2[3]), .carryin(adder_3_cout), .b(in_1[3]), .cout(out_4), .sum(out_5[3]));
endmodule

module overflow (
  input  a,
  input  b,
  input  OP,
  input  R3,
  output overflow
);

  wire and_1_out, and_2_out, not_1_out, not_2_out, xor_1_out;

  xor xor_1 (xor_1_out, b, OP);
  not not_1 (not_1_out, a);
  and and_1 (and_1_out, not_1_out, xor_1_out, R3);
  and and_2 (and_2_out, a, xor_1_out, not_2_out);
  not not_2 (not_2_out, R3);
  or or_1 (overflow, and_1_out, and_2_out);
endmodule
